# Fritzing sketch Automatic Light Source Tracking (saved by Fritzing 0.8.7b)

parts:
  R1 = Resistor [tolerance=±5% resistance=220 package=THT]
  R2 = Photocell (LDR) [package=THT]
  元件1 = SunFounder Uno R3
  J1 = Basic Servo

nets:
  N1: R1.Pin_0, R2.pin_1, 元件1.A0
  GND: R1.Pin_1, 元件1.GND, J1.gnd
  5V: R2.pin_0, 元件1.5V, J1.vcc
  N2: 元件1.D9_PWM, J1.pulse

custom parts:
  SunFounder Uno R3: The Arduino Uno is a microcontroller board based on the ATmega328 (datasheet). It has 14 digital input/output pins (of which 6 can be used as PWM outputs), 6 analog inputs, a 16 MHz ceramic resonator, a USB connection, a power jack, an ICSP header, and a reset button. It contains everything needed to support the microcontroller; simply connect it to a computer with a USB cable or power it with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
