# Fritzing sketch Light Alarm (saved by Fritzing 0.9.1b)
breadboards: 1

parts:
  J1 = Piezo Speaker
  Q1 = NPN-Transistor [package="TO92 [THT]"]
  R1 = Resistor [tolerance=±5% resistance=10k package=THT]
  LED1 = LED - 5mm [color="Red (633nm)" package="5 mm [THT]"]
  元件1 = SunFounder Uno R3

nets:
  N1: J1.pin1, R1.Pin_1, LED1.cathode, 元件1.GND
  N2: J1.pin2, 元件1.D5_PWM
  N3: Q1.E, 元件1.5V
  N4: Q1.B, LED1.anode
  N5: Q1.C, R1.Pin_0, 元件1.A0

custom parts:
  SunFounder Uno R3: The Arduino Uno is a microcontroller board based on the ATmega328 (datasheet). It has 14 digital input/output pins (of which 6 can be used as PWM outputs), 6 analog inputs, a 16 MHz ceramic resonator, a USB connection, a power jack, an ICSP header, and a reset button. It contains everything needed to support the microcontroller; simply connect it to a computer with a USB cable or power it with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
