# Fritzing sketch relay (saved by Fritzing 0.8.7b)
breadboards: 1

parts:
  K1 = Relay [part_number=FRS1B-S package=THT]
  Q1 = NPN-Transistor [package="TO92 [THT]"]
  R1 = Resistor [tolerance=±5% resistance=1k package=THT]
  R2 = Resistor [tolerance=±5% resistance=220 package=THT]
  D1 = Rectifier Diode [part_number=1N4001 package="300 mil [THT]"]
  LED1 = LED - 5mm [color="Red (633nm)" package="5 mm [THT]"]
  元件1 = Arduino Uno (Rev3) - ICSP

nets:
  N1: K1.COIL1, K1.C1, K1.C2, D1.cathode, 元件1.5V
  N2: K1.COIL2, Q1.C, D1.anode
  N3: K1.B, R2.Pin_0
  N4: Q1.E, LED1.cathode, 元件1.GND
  N5: Q1.B, R1.Pin_0
  N6: R1.Pin_1, 元件1.D8
  N7: R2.Pin_1, LED1.anode
